# Fritzing sketch PlabackBot (saved by Fritzing 0.9.3b)
breadboards: 1

parts:
  Part1 = Arduino Uno (Rev3) - ICSP
  J2 = Basic Servo
  J3 = Basic Servo
  R1 = Rotary Potentiometer (Large) [maximum_resistance=100kΩ package=THT]
  R2 = Rotary Potentiometer (Large) [maximum_resistance=100kΩ package=THT]

nets:
  N1: Part1.A0, R2.wiper
  N2: Part1.A2, R1.wiper
  N3: Part1.D9_PWM, J2.pulse
  N4: Part1.D10_PWM/SS, J3.pulse
  GND: Part1.GND, J2.gnd, J3.gnd, R1.leg1, R2.leg1
  5V: Part1.5V, J2.vcc, R1.leg2, R2.leg2
